# Fritzing sketch Scrarecrow (saved by Fritzing 0.9.8b)
breadboards: 1

parts:
  Part1 = Arduino Uno (Rev3)
  Micro_servo_sg90 = Tower Pro SG90 servo [part_number="Left arm"]
  Micro_servo_sg90_2 = Tower Pro SG90 servo [part_number="Right arm"]
  Micro_servo_sg90_3 = Tower Pro SG90 servo [part_number="Left leg"]
  Micro_servo_sg90_4 = Tower Pro SG90 servo [part_number="Right leg"]

nets:
  N1: Part1.D9_PWM, Micro_servo_sg90_2.Signal
  N2: Part1.D10_PWM/SS, Micro_servo_sg90.Signal
  N3: Part1.D11_PWM/MOSI, Micro_servo_sg90_4.Signal
  N4: Part1.D12/MISO, Micro_servo_sg90_3.Signal
  +5V: Part1.5V, Micro_servo_sg90.+5V, Micro_servo_sg90_2.+5V, Micro_servo_sg90_3.+5V, Micro_servo_sg90_4.+5V
  GND: Part1.GND, Micro_servo_sg90.GND, Micro_servo_sg90_2.GND, Micro_servo_sg90_3.GND, Micro_servo_sg90_4.GND

custom parts:
  Tower Pro SG90 servo: Original file by John De Cristofaro http://www.adafruit.com/products/1449 Adafruit Feedback Servo (Small) Edited by: e-radionica.com 28/9/2015
