# Fritzing sketch Measurement oxygen sketch (saved by Fritzing 0.9.8b)
breadboards: 2

parts:
  Part1 = Arduino Uno (Rev3)
  LCD2004-I2C1 = LCD2004-I2C
  A1 = PH meter

nets:
  N1: Part1.A4/SDA, LCD2004-I2C1.SDA
  N2: Part1.A5/SCL, LCD2004-I2C1.SCL
  5V: Part1.5V, LCD2004-I2C1.VCC, A1.pin2
  GND: Part1.GND, LCD2004-I2C1.GND, A1.pin1

custom parts:
  LCD2004-I2C: A standard character display with 4x20 characters. Comes in many colors with LCM2004 IIC attached.
  PH meter: DFrobot Dissolved Oxygen meter (SKU SEN0237A)
