# Fritzing sketch Overview of the system diagram Sketch (saved by Fritzing 0.9.8b)
breadboards: 1

parts:
  Scarcorw_(Slave) = Arduino Uno (Rev3) [part_number="arduino uno"]
  Clam_cage_(Slave) = Arduino Uno (Rev3) [part_number="arduino uno"]
  Oxygen_meter_(Master) = Arduino Uno (Rev3) [part_number="arduino uno"]
  Api_(Slave) = MKR1000 [part_number=Mkr1010]

nets:
  N1: Scarcorw_(Slave).A4/SDA, Clam_cage_(Slave).A4/SDA, Oxygen_meter_(Master).A4/SDA, Api_(Slave).connector56
  N2: Clam_cage_(Slave).A5/SCL, Oxygen_meter_(Master).A5/SCL, Api_(Slave).connector55
